# Fritzing sketch Arduino_Interrupt_fritzing (saved by Fritzing 0.9.3b)
breadboards: 1

parts:
  Parça1 = Arduino Nano (Rev3.0)
  R1 = Resistor [tolerance=±5% resistance=220 package=THT]
  R2 = Resistor [tolerance=±5% resistance=220 package=THT]
  R3 = Resistor [tolerance=±5% resistance=220 package=THT]
  R4 = Resistor [tolerance=±5% resistance=220 package=THT]
  LED1 = LED - 5mm [color="Red (633nm)" package="5 mm [THT]"]
  LED2 = LED - 5mm [color="Green (570nm)" package="5 mm [THT]"]
  LED3 = LED - 5mm [color="Yellow (592nm)" package="5 mm [THT]"]
  LED4 = LED - 5mm [color="Blue (470nm)" package="5 mm [THT]"]
  S1 = Pushbutton [package="[THT]"]
  R5 = Resistor [tolerance=±5% resistance=10k package=THT]

nets:
  N1: Parça1.GND, LED1.cathode, LED2.cathode, LED3.cathode, LED4.cathode, R5.Pin_1
  N2: Parça1.D2, S1.Pin_1, S1.Pin_2, R5.Pin_0
  N3: Parça1.D5, R2.Pin_1
  N4: Parça1.D6, R3.Pin_1
  N5: Parça1.D7, R4.Pin_1
  N6: Parça1.D8, R1.Pin_1
  N7: Parça1.5V, S1.Pin_3, S1.Pin_4
  N8: R1.Pin_0, LED2.anode
  N9: R2.Pin_0, LED4.anode
  N10: R3.Pin_0, LED1.anode
  N11: R4.Pin_0, LED3.anode

notes:
  Arduino Nano Interrupt Pinleri 2 ve 3. pinler, butonu istediginiz bir pine baglayabilirsiniz.
