# Fritzing sketch Cisim_Sayici_Proje_fritzing (saved by Fritzing 0.9.3b)
breadboards: 1

parts:
  Parça1 = Arduino Uno (Rev3)
  M1 = fc-51 [package=THT]
  LED1 = LED - 5mm [color="Red (633nm)" package="5 mm [THT]"]
  R1 = Resistor [tolerance=±5% resistance=220 package=THT]

nets:
  N1: Parça1.D8, M1.pin1
  N2: Parça1.D12/MISO, LED1.anode
  N3: Parça1.5V, M1.pin3
  N4: Parça1.GND, M1.pin2, R1.Pin_0
  N5: LED1.cathode, R1.Pin_1

notes:
  IR sensoru videonun altindaki linkten indirebilirsiniz.
