# Fritzing sketch Manyetik_Sensör_Kullanımı_fritzing (saved by Fritzing 0.9.3b)
breadboards: 1

parts:
  LED1 = LED - 5mm [color="Red (633nm)" package="5 mm [THT]"]
  J1 = Piezo Speaker
  Part1 = KY-024 Linear Hall Magnetic Sensor Module [package="Breakout board"]
  Parça1 = Arduino Nano (Rev3.0)

nets:
  N1: LED1.cathode, J1.pin1, Part1.G, Parça1.GND
  N2: LED1.anode, Parça1.D9
  N3: J1.pin2, Parça1.D6
  N4: Part1.+, Parça1.5V
  N5: Part1.D0, Parça1.D2

custom parts:
  KY-024 Linear Hall Magnetic Sensor Module: KEYES KY-024 Arduino Linear Hall Magnetic Sensor Module reacts iin the presence of a magnetic field.
