# Fritzing sketch Nem Sensorü Fritzing (saved by Fritzing 0.9.3b)
breadboards: 1

parts:
  R1 = Resistor [tolerance=±5% resistance=220 package=THT]
  R2 = Resistor [tolerance=±5% resistance=220 package=THT]
  R3 = Resistor [tolerance=±5% resistance=220 package=THT]
  LED1 = LED - 5mm [color="Red (633nm)" package="5 mm [THT]"]
  LED2 = LED - 5mm [color="Yellow (585nm)" package="5 mm [THT]"]
  LED3 = LED - 5mm [color="Green (560nm)" package="5 mm [THT]"]
  Parça1 = FC-28 Soil Hygrometer Module - Probe
  Parça2 = FC-28 Soil Hygrometer Module
  Parça3 = Arduino Uno (Rev3)

nets:
  GND: R1.Pin_0, R2.Pin_0, R3.Pin_0, Parça2.GND, Parça3.GND
  N1: R1.Pin_1, LED3.cathode
  N2: R2.Pin_1, LED2.cathode
  N3: R3.Pin_1, LED1.cathode
  N4: LED1.anode, Parça3.D9_PWM
  N5: LED2.anode, Parça3.D8
  N6: LED3.anode, Parça3.D7
  N7: Parça1.POS, Parça2.POS
  N8: Parça1.NEG, Parça2.NEG
  VCC: Parça2.VCC, Parça3.5V
  N9: Parça2.AO, Parça3.A0

notes:
  Toprak Nem Sensörünü videonun altındaki linkten bulabilirsiniz.

custom parts:
  FC-28 Soil Hygrometer Module - Probe: The FC-28 is a soil hygrometer module that uses the Texas Instruments LM393 comparator chip to provide an analog measurement of soil humidity.
  FC-28 Soil Hygrometer Module: The FC-28 is a soil hygrometer module that uses the Texas Instruments LM393 comparator chip to provide an analog measurement of soil humidity. The digital output is high when soil moisture is over a certain threshold, as determined by adjusting the potentiometer.
