# Fritzing sketch PiezoSensorFritzing (saved by Fritzing 0.9.3b)
breadboards: 1

parts:
  LED1 = LED - 5mm [color="White (4500K)" package="5 mm [THT]"]
  Parça1 = Arduino Uno (Rev3)
  Piezoelectric_Sensor1 = Piezoelectric Sensor

nets:
  GND: LED1.cathode, Parça1.GND, Piezoelectric_Sensor1.GND
  N1: LED1.anode, Parça1.D13/SCK
  N2: Parça1.A0, Piezoelectric_Sensor1.VCC

notes:
  Piezo sensörü videonun altındaki linkten indirebilirsiniz.

custom parts:
  Piezoelectric Sensor: Piezoelectric sensor.
