# Fritzing sketch dht11_fritzing (saved by Fritzing 0.9.3b)
breadboards: 1

parts:
  Parça1 = Arduino Uno (Rev3)
  R1 = Resistor [tolerance=±5% resistance=220 package=THT]
  R2 = Resistor [tolerance=±5% resistance=220 package=THT]
  LED1 = LED - 5mm [color="Red (633nm)" package="5 mm [THT]"]
  LED2 = LED - 5mm [color="Green (570nm)" package="5 mm [THT]"]
  Part1 = KY-015 Temperature & Humidity Sensor Module [package="Breakout board"]
  M1 = DC Motor

nets:
  N1: Parça1.D8, M1.pin_2
  N2: Parça1.D12/MISO, LED2.anode
  N3: Parça1.D13/SCK, LED1.anode
  N4: Parça1.D2, Part1.S
  5V: Parça1.5V, Part1.Vin
  N5: Parça1.GND, R1.Pin_0, R2.Pin_0, Part1.-, M1.pin_1
  N6: R1.Pin_1, LED2.cathode
  N7: R2.Pin_1, LED1.cathode

notes:
  DHT11 parçasını videonun altındaki linkten indirebilirsiniz.

custom parts:
  KY-015 Temperature & Humidity Sensor Module: KY-015 temperature and humidity sensor module, provides a low-latency serial interface to measure humidity and temperature.
