# Fritzing sketch ds3231_fritzing (saved by Fritzing 0.9.3b)

parts:
  Parça1 = Arduino Uno (Rev3)
  ZS-042_RTC1 = ZS-042 RTC Module

nets:
  N1: Parça1.A4/SDA, ZS-042_RTC1.SDA
  N2: Parça1.A5/SCL, ZS-042_RTC1.SCL
  5V: Parça1.5V, ZS-042_RTC1.VCC
  GND: Parça1.GND, ZS-042_RTC1.GND
