# Fritzing sketch fire_alarm_frit (saved by Fritzing 0.9.3b)
breadboards: 1

parts:
  Part1 = KY-026 Flame Sensor Module [package="Breakout board"]
  R1 = Resistor [tolerance=±5% resistance=220 package=THT]
  Parça1 = Arduino Nano (Rev3.0)
  LED1 = LED - 5mm [color="Red (633nm)" package="5 mm [THT]"]
  J1 = Piezo Speaker

nets:
  N1: Part1.G, Parça1.GND, LED1.cathode, J1.pin1
  N2: Part1.+, Parça1.5V
  N3: Part1.D0, Parça1.D2
  N4: R1.Pin_0, LED1.anode
  N5: R1.Pin_1, Parça1.D3
  N6: Parça1.D4, J1.pin2

custom parts:
  KY-026 Flame Sensor Module: KEYES KY-026 Arduino Flame Sensor Module reacts iin the presence of fire.
