# Fritzing sketch fritzing_servo_with_gyroskop (saved by Fritzing 0.9.3b)
breadboards: 2

parts:
  GY1 = GY-521 (MPU-6050) [form="♀ (female)" package=THT]
  J1 = Basic Servo
  J2 = Basic Servo
  Parça1 = Arduino Uno (Rev3)
  VCC1 = Battery block 9V

nets:
  N1: GY1.pin1, Parça1.5V
  GND: GY1.pin2, J1.gnd, J2.gnd, Parça1.GND, VCC1.-
  N2: GY1.pin3, Parça1.A5/SCL
  N3: GY1.pin4, Parça1.A4/SDA
  VCC: J1.vcc, J2.vcc, VCC1.+
  N4: J1.pulse, Parça1.D9_PWM
  N5: J2.pulse, Parça1.D8

custom parts:
  GY-521 (MPU-6050): Placa GY-521 basada en conjunto de acelerómetro+giroscopios MPU-6050
