# Fritzing sketch gy_fritzing (saved by Fritzing 0.9.3b)

parts:
  GY1 = GY-521 (MPU-6050) [form="♀ (female)" package=THT]
  Parça1 = Arduino Uno (Rev3)

nets:
  N1: GY1.pin1, Parça1.5V
  N2: GY1.pin2, Parça1.GND
  N3: GY1.pin3, Parça1.A5/SCL
  N4: GY1.pin4, Parça1.A4/SDA

notes:
  SLC=Serial Clock Line
  SDA=Serial DataLine
  XDA=Auxilary Data
  XCL=Auxilary Clock
  ADO=Address Output
  INT=Interrupt (kesme durdurma)
  VCC=5V
  GND=GND
  SLC=SLC ARDUNODAKİ
  SDA=SDA ARDUİNODAKİ
  DİĞER PİNLER BOŞ

custom parts:
  GY-521 (MPU-6050): Placa GY-521 basada en conjunto de acelerómetro+giroscopios MPU-6050
