# Fritzing sketch l293d_fritzing (saved by Fritzing 0.9.3b)
breadboards: 1

parts:
  Parça1 = Arduino Uno (Rev3)
  IC1 = L293D [package=THT]
  R1 = Resistor [tolerance=±5% resistance=220 package=THT]
  R2 = Resistor [tolerance=±5% resistance=220 package=THT]
  LED1 = LED - 5mm [color="Red (633nm)" package="5 mm [THT]"]
  LED2 = LED - 5mm [color="Green (570nm)" package="5 mm [THT]"]
  M1 = DC Motor
  VCC1 = 4 x AAA Battery Mount

nets:
  N1: Parça1.D8, LED1.anode
  N2: Parça1.GND, IC1.0V, R1.Pin_0, R2.Pin_0, VCC1.-
  N3: Parça1.D2, IC1.Enable_1
  N4: Parça1.D3_PWM, IC1.In_1
  N5: Parça1.D4, IC1.In_2
  N6: Parça1.D7, LED2.anode
  N7: IC1.Out_1_(_Controlled_by_Enable_1_), M1.pin_2
  N8: IC1.Out_2_(_Controlled_by_Enable_1_), M1.pin_1
  N9: IC1.+Vmotor, VCC1.+
  N10: R1.Pin_1, LED2.cathode
  N11: R2.Pin_1, LED1.cathode
