# Fritzing sketch laser.fritzing (saved by Fritzing 0.9.3b)
breadboards: 1

parts:
  R1 = Resistor [tolerance=±5% resistance=220 package=THT]
  R2 = Resistor [tolerance=±5% resistance=220 package=THT]
  LED1 = LED - 5mm [color="Green (570nm)" package="5 mm [THT]"]
  LED2 = LED - 5mm [color="Red (633nm)" package="5 mm [THT]"]
  J1 = Piezo Speaker
  R3 = Resistor [tolerance=±5% resistance=1k package=THT]
  R4 = Photocell (LDR) [package=THT]
  R5 = Resistor [tolerance=±5% resistance=1k package=THT]
  Parça1 = Arduino Uno (Rev3)
  LD1 = LD

nets:
  N1: R1.Pin_0, R2.Pin_0, R3.Pin_1, R4.pin_0, Parça1.GND, LD1.cathode
  N2: R1.Pin_1, LED2.cathode
  N3: R2.Pin_1, LED1.cathode
  N4: LED1.anode, Parça1.D9_PWM
  N5: LED2.anode, Parça1.D8
  N6: J1.pin1, R3.Pin_0
  N7: J1.pin2, Parça1.D10_PWM/SS
  N8: R4.pin_1, R5.Pin_0, Parça1.A0
  N9: R5.Pin_1, Parça1.5V, LD1.anode

notes:
  Kullandigimiz laser 3 bacakli oldugu icin bir bacagi biz ekledik.

custom parts:
  LD: A Generic Red Dot Laser Diode Module (~5mW)
