# Fritzing sketch laser_silah_fritzing (saved by Fritzing 0.9.3b)
breadboards: 1

parts:
  J1 = Basic Servo
  J2 = Basic Servo
  LED1 = LED - 5mm [color="Red (633nm)" package="5 mm [THT]"]
  LED2 = LED - 5mm [color="Green (570nm)" package="5 mm [THT]"]
  R1 = Resistor [tolerance=±5% resistance=220 package=THT]
  R2 = Resistor [tolerance=±5% resistance=220 package=THT]
  J3 = Piezo Speaker
  R3 = Resistor [tolerance=±5% resistance=1k package=THT]
  Parça1 = Thumb Joystick
  LD1 = LD
  BAT1 = BC9VPC [package=bc9vpc]
  Parça2 = Arduino Uno (Rev3)

nets:
  GND: J1.gnd, Parça1.GND, LD1.cathode, BAT1.V-, Parça2.GND
  N1: J1.vcc, BAT1.V+
  N2: J1.pulse, Parça2.D9_PWM
  N3: J2.pulse, Parça2.D8
  N4: LED1.cathode, R1.Pin_1
  N5: LED1.anode, Parça2.D13/SCK
  N6: LED2.cathode, R2.Pin_1
  N7: LED2.anode, Parça2.D12/MISO
  VCC: R1.Pin_0, R2.Pin_0, R3.Pin_0, Parça1.VCC, LD1.anode, Parça2.5V
  N8: J3.pin1, R3.Pin_1
  N9: J3.pin2, Parça2.D11_PWM/MOSI
  N10: Parça1.SEL, Parça2.D7
  N11: Parça1.HORZ, Parça2.A1
  N12: Parça1.VERT, Parça2.A0

notes:
  laserimiz 3 pinli olduğu için ortaya bir pin ekledik.

custom parts:
  LD: A Generic Red Dot Laser Diode Module (~5mW)
