# Fritzing sketch line tracking Sensor (saved by Fritzing 0.9.3b)
breadboards: 1

parts:
  Parça1 = Arduino Uno (Rev3)
  Parça2 = KY-033 Tracing Black White Line Hunting Sensor Module For Arduino
  R1 = Resistor [tolerance=±5% resistance=220 package=THT]
  R2 = Resistor [tolerance=±5% resistance=220 package=THT]
  LED1 = LED - 5mm [color="Red (633nm)" package="5 mm [THT]"]
  LED2 = LED - 5mm [color="Red (633nm)" package="5 mm [THT]"]

nets:
  N1: Parça1.D8, LED1.anode
  N2: Parça1.D9_PWM, LED2.anode
  N3: Parça1.D12/MISO, Parça2.S
  N4: Parça1.5V, Parça2.V+
  GND: Parça1.GND, Parça2.GND, R1.Pin_1, R2.Pin_1
  N5: R1.Pin_0, LED1.cathode
  N6: R2.Pin_0, LED2.cathode

notes:
  line tracking sensörün linkini videonun altındaki linkten bulabilirsiniz.

custom parts:
  KY-033 Tracing Black White Line Hunting Sensor Module For Arduino: Tracing Black White Line Hunting Sensor Module For Arduino Description: This is KY-033 tracking sensor. The KY-033 measures the intensity of infrared radiation and delivers it as an analog output voltage. Features: Operating voltage: 2.5 - 12V(cannot over12V) working current: 18mA-20mA at 5V Enhanced accuracy Documents: http://www.vishay.com/docs/83760/tcrt5000.pdf
