# Fritzing sketch rfid_fritzing (saved by Fritzing 0.9.3b)
breadboards: 1

parts:
  Parça1 = RFID-RC522 [part_number=101218]
  Parça2 = Arduino Uno (Rev3)
  R1 = Resistor [tolerance=±5% resistance=220 package=THT]
  R2 = Resistor [tolerance=±5% resistance=220 package=THT]
  LED1 = LED - 5mm [color="Red (633nm)" package="5 mm [THT]"]
  LED2 = LED - 5mm [color="Green (570nm)" package="5 mm [THT]"]
  J1 = Basic Servo

nets:
  N1: Parça1.SDA, Parça2.D10_PWM/SS
  N2: Parça1.SCK, Parça2.D13/SCK
  N3: Parça1.MOSI, Parça2.D11_PWM/MOSI
  N4: Parça1.MISO, Parça2.D12/MISO
  GND: Parça1.GND, Parça2.GND, R1.Pin_1, R2.Pin_1, J1.gnd
  N5: Parça1.RST, Parça2.D9_PWM
  3.3V: Parça1.3.3V, Parça2.3V3
  N6: Parça2.D2, LED2.anode
  N7: Parça2.D3_PWM, LED1.anode
  N8: Parça2.D7, J1.pulse
  5V: Parça2.5V, J1.vcc
  N9: R1.Pin_0, LED1.cathode
  N10: R2.Pin_0, LED2.cathode

notes:
  RFID BAGLANTILARI
  VCC=3.3 V
  GND=GND
  RST=RESET=9.PIN
  MISO=MASTER IN SLAVE OUT=12.PIN
  MOSI=MASTER OUT SLAVE IN=11.PIN
  SCK=SERIAL CLOCK=13.PIN
  SDA=SERIALDATA=10.PIN
  FRITZING PARCASINI VIDEONUN ALTINDAKI LINTEN INDIREBILIRSINIZ.
