# Fritzing sketch rotary_encoder_fritzing (saved by Fritzing 0.9.3b)
breadboards: 1

parts:
  Parça1 = Arduino Nano (Rev3.0)
  ENCODER1 = Rotary Encoder with Knob
  LED1 = LED - 5mm [color="Red (633nm)" package="5 mm [THT]"]
  R1 = Resistor [tolerance=±5% resistance=220 package=THT]

nets:
  N1: Parça1.GND, ENCODER1.no_name_yet#4, LED1.cathode
  N2: Parça1.D2, ENCODER1.no_name_yet#3
  N3: Parça1.D3, ENCODER1.no_name_yet#2
  N4: Parça1.D4, ENCODER1.no_name_yet#1
  N5: Parça1.D9, R1.Pin_1
  N6: Parça1.5V, ENCODER1.no_name_yet#5
  N7: LED1.anode, R1.Pin_0

notes:
  Rotary Encoder fritzing parcasini videonun altindaki linkten indirebilirsiniz. Rotary encoder ust bacaklar kirmizi vcc, siyah gnd olarak alinmistir. Alttaki sari kablo, clock yesil kablo data pini, beyaz kablo ise switch olarak alinmistir.

custom parts:
  Rotary Encoder with Knob: Rotary Encoder with 1/4" Shaft and Knob
