# Fritzing sketch sayı_tahmin_fritzing (saved by Fritzing 0.9.3b)
breadboards: 1

parts:
  Parça1 = Arduino Uno (Rev3)
  R1 = Resistor [tolerance=±5% resistance=1k package=THT]
  R2 = Resistor [tolerance=±5% resistance=1k package=THT]
  LED1 = LED - 5mm [color="Green (570nm)" package="5 mm [THT]"]
  LED2 = LED - 5mm [color="Red (633nm)" package="5 mm [THT]"]
  S1 = Momentary Switch [package=ksa_sealed_tac_switch]
  S2 = Momentary Switch [package=ksa_sealed_tac_switch]
  DI1 = 7-Segment LED Display [package=THT]
  R5 = Resistor [tolerance=±5% resistance=220 package=THT]
  R6 = Resistor [tolerance=±5% resistance=220 package=THT]
  R7 = Resistor [tolerance=±5% resistance=220 package=THT]
  R8 = Resistor [tolerance=±5% resistance=220 package=THT]
  R9 = Resistor [tolerance=±5% resistance=220 package=THT]
  R10 = Resistor [tolerance=±5% resistance=220 package=THT]
  R11 = Resistor [tolerance=±5% resistance=220 package=THT]
  R12 = Resistor [tolerance=±5% resistance=220 package=THT]
  R13 = Resistor [tolerance=±5% resistance=220 package=THT]

nets:
  N1: Parça1.D8, R9.Pin_1
  N2: Parça1.D9_PWM, S2.1
  N3: Parça1.D10_PWM/SS, S1.1
  N4: Parça1.D12/MISO, LED1.anode
  N5: Parça1.D13/SCK, LED2.anode
  N6: Parça1.D2, R5.Pin_0
  N7: Parça1.D4, R7.Pin_1
  N8: Parça1.D5_PWM, R10.Pin_0
  N9: Parça1.D6_PWM, R11.Pin_0
  N10: Parça1.D7, R8.Pin_1
  N11: Parça1.5V, S1.3, S2.3
  N12: Parça1.VIN, R1.Pin_1, R2.Pin_1, DI1.commAnode, R12.Pin_0, R13.Pin_0
  N13: R1.Pin_0, S1.2
  N14: R2.Pin_0, S2.2
  N15: LED1.cathode, R12.Pin_1
  N16: LED2.cathode, R13.Pin_1
  N17: DI1.cathodeE, R5.Pin_1
  N18: DI1.cathodeD, R6.Pin_1
  N19: DI1.cathodeC, R7.Pin_0
  N20: DI1.cathodeB, R8.Pin_0
  N21: DI1.cathodeA, R9.Pin_0
  N22: DI1.cathodeF, R11.Pin_1
  N23: DI1.cathodeG, R10.Pin_1
