# Fritzing sketch seven_segment_display_fritzing (saved by Fritzing 0.9.3b)
breadboards: 1

parts:
  R1 = Resistor [tolerance=±5% resistance=220 package=THT]
  R2 = Resistor [tolerance=±5% resistance=220 package=THT]
  R3 = Resistor [tolerance=±5% resistance=220 package=THT]
  R4 = Resistor [tolerance=±5% resistance=220 package=THT]
  R5 = Resistor [tolerance=±5% resistance=220 package=THT]
  R6 = Resistor [tolerance=±5% resistance=220 package=THT]
  R7 = Resistor [tolerance=±5% resistance=220 package=THT]
  DI1 = 7-Segment LED Display [package=THT]
  Parça1 = Arduino Uno (Rev3)

nets:
  N1: R1.Pin_0, DI1.cathodeB
  N2: R1.Pin_1, Parça1.D8
  N3: R2.Pin_0, DI1.cathodeA
  N4: R2.Pin_1, Parça1.D7
  N5: R3.Pin_0, Parça1.D5_PWM
  N6: R3.Pin_1, DI1.cathodeG
  N7: R4.Pin_0, Parça1.D6_PWM
  N8: R4.Pin_1, DI1.cathodeF
  N9: R5.Pin_0, DI1.cathodeC
  N10: R5.Pin_1, Parça1.D4
  N11: R6.Pin_0, Parça1.D3_PWM
  N12: R6.Pin_1, DI1.cathodeD
  N13: R7.Pin_0, Parça1.D2
  N14: R7.Pin_1, DI1.cathodeE
  N15: DI1.commAnode#2, Parça1.GND
