# Fritzing sketch thermistor.fritzing (saved by Fritzing 0.9.3b)
breadboards: 1

parts:
  Parça1 = Arduino Uno (Rev3)
  R1 = Resistor [tolerance=±5% resistance=10k package=THT]
  R2 = Temperature Sensor (Thermistor) [thermistor_type=NTC package=THT]

nets:
  N1: Parça1.A1, R1.Pin_0, R2.pin_1
  N2: Parça1.5V, R1.Pin_1
  N3: Parça1.GND, R2.pin_0
