# Fritzing sketch touch_sensorfritzing (saved by Fritzing 0.9.3b)
breadboards: 1

parts:
  TTP223B1 = TTP223B Capacitive Touch Sensor Module
  Parça1 = Arduino Uno (Rev3)
  R1 = Resistor [tolerance=±5% resistance=220 package=THT]
  R2 = Resistor [tolerance=±5% resistance=220 package=THT]
  R3 = Resistor [tolerance=±5% resistance=220 package=THT]
  LED1 = LED - 5mm [color="Red (633nm)" package="5 mm [THT]"]
  LED2 = LED - 5mm [color="Blue (470nm)" package="5 mm [THT]"]
  LED3 = LED - 5mm [color="Green (570nm)" package="5 mm [THT]"]

nets:
  GND: TTP223B1.GND, Parça1.GND
  VCC: TTP223B1.VCC, Parça1.3V3
  N1: TTP223B1.SIG, Parça1.D8
  N2: Parça1.D11_PWM/MOSI, LED1.anode
  N3: Parça1.D12/MISO, LED2.anode
  N4: Parça1.D13/SCK, LED3.anode
  N5: R1.Pin_0, LED1.cathode
  N6: R1.Pin_1, R2.Pin_1, R3.Pin_1
  N7: R2.Pin_0, LED2.cathode
  N8: R3.Pin_0, LED3.cathode

notes:
  Dokunmatik Sensörü videonun altındaki linkten indirebilirsiniz.

custom parts:
  TTP223B Capacitive Touch Sensor Module: The TTP223B capacitive touch sensor module uses the TTP223B IC. The appropriate voltage is approximately 2 to 5.5 volts.
